# Fritzing sketch weather-station (saved by Fritzing 0.9.3b)

parts:
  U1 = NodeMCU V3.0
  Temp_/_Humidity_/_Air_Pressure = BME280 Breakout
  Mod2 = SDS011 - dust sensor [part_number=1]  # not connected
  YL-83_-_Detection_Board2 = YL-83 Rain Sensor - Detection Board
  YL-83_-_Control_Board2 = YL-83 Rain Sensor - Control Board
  UV_Sensor = ML8511 UV Sensor Breakout [part_number=SEN-12705]
  Anemometer = DC Motor  # not connected
  Part3 = Analog Digital MUX Breakout

nets:
  N1: U1.D1, Temp_/_Humidity_/_Air_Pressure.SCK/SCL
  N2: U1.D2, Temp_/_Humidity_/_Air_Pressure.SDI/SDA
  N3: U1.D3, Part3.S2
  N4: U1.D4, Part3.S3
  3.3V: U1.3V3, Temp_/_Humidity_/_Air_Pressure.3.3V, YL-83_-_Control_Board2.VCC, UV_Sensor.3.3V, Part3.VCC
  GND: U1.GND, Temp_/_Humidity_/_Air_Pressure.GND, YL-83_-_Control_Board2.GND, UV_Sensor.GND, Part3.GND, Part3.EN
  N5: U1.D7, Part3.S1
  N6: U1.D8, Part3.S0
  N7: U1.A0, Part3.SIG
  N8: YL-83_-_Detection_Board2.POS, YL-83_-_Control_Board2.POS
  N9: YL-83_-_Detection_Board2.NEG, YL-83_-_Control_Board2.NEG
  N10: YL-83_-_Control_Board2.AO, Part3.C0
  N11: UV_Sensor.OUT, Part3.C1

custom parts:
  NodeMCU V3.0: ESP8266 based NodeMCU
  SDS011 - dust sensor: The SDS 011 Sensor is a quite recent Air Quality Sensor developed by inovafit, a spin-off from the university of Jinan (in Shandong). With its size, it is probably one of the best sensor in terms of accuracy: While other sensors tend to focus on shrinking the sensor size, the SDS 011 has opted for a size tradeoff allowing it to use a larger fan. And the larger the fan, the better the quality.
  YL-83 Rain Sensor - Detection Board: The YL-83 is a rain sensor that has more resistance when dry and less resistance when wet. The module runs at 5V.
  YL-83 Rain Sensor - Control Board: The YL-83 is a rain sensor that has more resistance when dry and less resistance when wet. The module runs at 5V.
  ML8511 UV Sensor Breakout: Description: The ML8511 breakout is an easy to use ultraviolet light sensor. The MP8511 UV Sensor works by outputing an analog signal in relation to the amount of UV light it detects. This breakout can be very handy in creating devices that warn the user of sunburn or detect the UV index as it relates to weather conditions. This sensor breakout can detect 280-390nm light most effectively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
